# Fritzing sketch DC motor (saved by Fritzing 0.9.3b)

parts:
  Part1 = gizDuino SE (Student Edition)
  Part2 = 2-CHANNEL TINY DC MOTOR DRIVER
  M1 = DC Motor  # not connected

nets:
  N1: Part1.D8, Part2.IN1
  N2: Part1.D9_PWM, Part2.IN2
  N3: Part1.D10_PWM/SS, Part2.IN3
  N4: Part1.D11_PWM/MOSI, Part2.IN4

custom parts:
  gizDuino SE (Student Edition): ATMEGA328P Arduino Uno Compatible This Arduino Uno Compatible board is built for low cost and is sold to STUDENTS/TEACHERS ONLY. - Uses the same core MCU ATMEGA328P - 100% Code compatible - CH340 USB to UART Bridge
  2-CHANNEL TINY DC MOTOR DRIVER: e-Gizmo 2 Channel Tiny Motor Driver is a simple motor driver board and small package based on A3906 Allegro's low voltage dual DC motor driver IC. It is designed for PWM control of low voltage motors.
