# Fritzing sketch LCDi2c (saved by Fritzing 0.9.3b)

parts:
  Part1 = gizDuino SE (Student Edition)
  JM162B_2X16_LCD_with_I2C_Serial_Interface1 = JM162B 2X16 LCD with I2C Serial Interface [part_number="JM162B 2X16 LCD with I2C Serial Interface" chip_label=IC package="DIP (Dual Inline) [THT]"]

nets:
  N1: Part1.A4/SDA, JM162B_2X16_LCD_with_I2C_Serial_Interface1.SDA
  N2: Part1.A5/SCL, JM162B_2X16_LCD_with_I2C_Serial_Interface1.SCL
  5V: Part1.5V, JM162B_2X16_LCD_with_I2C_Serial_Interface1.VCC
  GND: Part1.GND, JM162B_2X16_LCD_with_I2C_Serial_Interface1.GND

custom parts:
  gizDuino SE (Student Edition): ATMEGA328P Arduino Uno Compatible This Arduino Uno Compatible board is built for low cost and is sold to STUDENTS/TEACHERS ONLY. - Uses the same core MCU ATMEGA328P - 100% Code compatible - CH340 USB to UART Bridge
  JM162B 2X16 LCD with I2C Serial Interface: 16 Characters x 2 lines LCD display with I2C interface module, where you will be able to realize data display via only 2 wires.
