# Fritzing sketch Switch (saved by Fritzing 0.9.3b)
breadboards: 1

parts:
  Part1 = gizDuino SE (Student Edition)
  S1 = Pushbutton [package=THT]
  S2 = Pushbutton [package=THT]
  R1 = Resistor [tolerance=±5% resistance=10k package="0603 [SMD]"]
  R2 = Resistor [tolerance=±5% resistance=10k package="0603 [SMD]"]
  R3 = Resistor [tolerance=±5% resistance=470 package="0603 [SMD]"]
  R4 = Resistor [tolerance=±5% resistance=470 package="0603 [SMD]"]
  LED1 = smd LED [color="Red (633nm)" package="0805 [SMD]"]
  LED2 = smd LED [color="Blue (430nm)" package="0805 [SMD]"]

nets:
  N1: Part1.D10_PWM/SS, LED1.anode
  N2: Part1.D11_PWM/MOSI, LED2.anode
  N3: Part1.D2, S2.leg0, R2.Pin_0
  N4: Part1.D3_PWM, S1.leg0, R1.Pin_0
  N5: Part1.5V, R1.Pin_1, R2.Pin_1
  N6: Part1.GND, S1.leg1, S2.leg1, R3.Pin_0, R4.Pin_0
  N7: R3.Pin_1, LED2.cathode
  N8: R4.Pin_1, LED1.cathode

custom parts:
  gizDuino SE (Student Edition): ATMEGA328P Arduino Uno Compatible This Arduino Uno Compatible board is built for low cost and is sold to STUDENTS/TEACHERS ONLY. - Uses the same core MCU ATMEGA328P - 100% Code compatible - CH340 USB to UART Bridge
