# Fritzing sketch blink (saved by Fritzing 0.9.3b)
breadboards: 1

parts:
  Part1 = gizDuino SE (Student Edition)
  LED1 = LED - 3mm [color="Blue (430nm)" package="3 mm [THT]"]
  R1 = Resistor [tolerance=±5% resistance=470 package="0603 [SMD]"]

nets:
  N1: Part1.D13/SCK, R1.Pin_1
  N2: Part1.GND, LED1.cathode
  N3: LED1.anode, R1.Pin_0

custom parts:
  gizDuino SE (Student Edition): ATMEGA328P Arduino Uno Compatible This Arduino Uno Compatible board is built for low cost and is sold to STUDENTS/TEACHERS ONLY. - Uses the same core MCU ATMEGA328P - 100% Code compatible - CH340 USB to UART Bridge
