# Fritzing sketch buzzer (saved by Fritzing 0.9.3b)
breadboards: 1

parts:
  Part1 = gizDuino SE (Student Edition)
  Part2 = HIGH QUALITY PASSIVE BUZZER MODULE

nets:
  N1: Part1.D9_PWM, Part2.I/O
  5V: Part1.5V, Part2.VCC
  GND: Part1.GND, Part2.GND

custom parts:
  gizDuino SE (Student Edition): ATMEGA328P Arduino Uno Compatible This Arduino Uno Compatible board is built for low cost and is sold to STUDENTS/TEACHERS ONLY. - Uses the same core MCU ATMEGA328P - 100% Code compatible - CH340 USB to UART Bridge
  HIGH QUALITY PASSIVE BUZZER MODULE: This passive buzzer module has a built-in driver, hence you can connect its input directly to a has controller. Note that this is not a stand alone buzzer, it requires a driving signal form a host controller. This buzzer is at its loudest when driven with a 2Khz-5KHz square wave. Compatible with all gizDuino and Arduino Boards.
