# Fritzing sketch dht (saved by Fritzing 0.9.3b)

parts:
  Part1 = gizDuino SE (Student Edition)
  DHT1 = HUMIDITY: DHT11 Breakout Board [part_number=DHT11 chip_label=IC package="DIP (Dual Inline) [THT]"]

nets:
  N1: Part1.D12/MISO, DHT1.OUT
  N2: Part1.5V, DHT1.+VCC
  GND: Part1.GND, DHT1.GND

custom parts:
  gizDuino SE (Student Edition): ATMEGA328P Arduino Uno Compatible This Arduino Uno Compatible board is built for low cost and is sold to STUDENTS/TEACHERS ONLY. - Uses the same core MCU ATMEGA328P - 100% Code compatible - CH340 USB to UART Bridge
  HUMIDITY: DHT11 Breakout Board: DHT11 Temperature & Humidity Sensor features a temperature & humidity sensor complex with a calibrated digital signal output. By using the exclusive digital-signal-acquisition technique and temperature & humidity sensing technology, it ensures high reliability and excellent long-term stability. This sensor includes a resistive-type humidity measurement component and an NTC temperature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
