# Fritzing sketch multipleLED (saved by Fritzing 0.9.3b)
breadboards: 1

parts:
  Part1 = gizDuino SE (Student Edition)
  R1 = Resistor [tolerance=±5% resistance=470 package="2010 [SMD]"]
  R2 = Resistor [tolerance=±5% resistance=470 package="0603 [SMD]"]
  LED1 = LED - 3mm [color="Blue (430nm)" package="3 mm [THT]"]
  LED2 = LED - 3mm [color="Blue (430nm)" package="3 mm [THT]"]
  LED3 = LED - 3mm [color="Blue (430nm)" package="3 mm [THT]"]
  LED4 = LED - 3mm [color="Blue (430nm)" package="3 mm [THT]"]
  LED5 = LED - 3mm [color="Blue (430nm)" package="3 mm [THT]"]
  R3 = Resistor [tolerance=±5% resistance=470 package="0603 [SMD]"]
  R4 = Resistor [tolerance=±5% resistance=470 package="0603 [SMD]"]
  R5 = Resistor [tolerance=±5% resistance=470 package=THT]

nets:
  N1: Part1.GND, LED1.cathode, LED2.cathode, LED3.cathode, LED4.cathode, LED5.cathode
  N2: Part1.D8, R1.Pin_0
  N3: Part1.D9_PWM, R2.Pin_0
  N4: Part1.D11_PWM/MOSI, R4.Pin_0
  N5: Part1.D12/MISO, R5.Pin_0
  N6: R1.Pin_1, LED1.anode
  N7: R2.Pin_1, LED2.anode
  N8: LED3.anode, R3.Pin_1
  N9: LED4.anode, R4.Pin_1
  N10: LED5.anode, R5.Pin_1

custom parts:
  gizDuino SE (Student Edition): ATMEGA328P Arduino Uno Compatible This Arduino Uno Compatible board is built for low cost and is sold to STUDENTS/TEACHERS ONLY. - Uses the same core MCU ATMEGA328P - 100% Code compatible - CH340 USB to UART Bridge
