# Fritzing sketch relay (saved by Fritzing 0.9.3b)

parts:
  Part1 = gizDuino SE (Student Edition)
  Part2 = RELAY MODULE 5V

nets:
  GND: Part1.GND, Part2.GND
  N1: Part1.D5_PWM, Part2.IN
  5V: Part1.5V, Part2.VCC

custom parts:
  gizDuino SE (Student Edition): ATMEGA328P Arduino Uno Compatible This Arduino Uno Compatible board is built for low cost and is sold to STUDENTS/TEACHERS ONLY. - Uses the same core MCU ATMEGA328P - 100% Code compatible - CH340 USB to UART Bridge
  RELAY MODULE 5V: 5V Relay module with 10A contact - Buffered input (Active Low) - LED Indicators - NO/NC Terminals - 220VAC Rated Contacts
