# Fritzing sketch servo (saved by Fritzing 0.9.3b)

parts:
  Part1 = gizDuino SE (Student Edition)
  J1 = Basic Servo

nets:
  N1: Part1.D9_PWM, J1.pulse
  5V: Part1.5V, J1.vcc
  GND: Part1.GND, J1.gnd

custom parts:
  gizDuino SE (Student Edition): ATMEGA328P Arduino Uno Compatible This Arduino Uno Compatible board is built for low cost and is sold to STUDENTS/TEACHERS ONLY. - Uses the same core MCU ATMEGA328P - 100% Code compatible - CH340 USB to UART Bridge
