# Fritzing sketch us100 (saved by Fritzing 0.9.3b)

parts:
  Part1 = gizDuino SE (Student Edition)
  hc-sr1 = hc-sr04

nets:
  N1: Part1.D11_PWM/MOSI, hc-sr1.Trig
  N2: Part1.D12/MISO, hc-sr1.Echo
  5V: Part1.5V, hc-sr1.VCC
  GND: Part1.GND, hc-sr1.GND

custom parts:
  gizDuino SE (Student Edition): ATMEGA328P Arduino Uno Compatible This Arduino Uno Compatible board is built for low cost and is sold to STUDENTS/TEACHERS ONLY. - Uses the same core MCU ATMEGA328P - 100% Code compatible - CH340 USB to UART Bridge
